// Logisim project CPU_I.circ as structural Verilog: 1 circuit, main circuit main
module main (
  input  in_1,
  input  [23:0] in_2
);

  wire button_1_out, clock_1_out, comparator_1_eq;
  wire [3:0] controlled_buffer_1_out, rom_1_data_2, rom_1_data_3;
  wire [23:0] counter_1_q, rom_1_data;

  Clock clock_1 (.out(clock_1_out));
  Button button_1 (.out(button_1_out));
  Counter #(.max('hffffff), .width(24)) counter_1 (
    .load(in_1), .D(in_2), .count(1'b1), .Q(counter_1_q), .up(1'b1), .clk(clock_1_out), .clr(button_1_out));  // open: carry
  ROM #(.addrWidth(24), .dataWidth(32)) rom_1 (.addr(counter_1_q), .data({rom_1_data_3, rom_1_data_2, rom_1_data}));
  Comparator #(.width(4)) comparator_1 (.a(rom_1_data_3), .b(4'b0001), .eq(comparator_1_eq));  // open: gt, lt
  assign controlled_buffer_1_out = comparator_1_eq ? rom_1_data_2 : 4'bz;  // Controlled_Buffer controlled_buffer_1
  Pull_Resistor pull_resistor_1 (.node(rom_1_data_2));

  // Notes on the sheet:
  //   contents of rom_1 (hex, n*v repeats v):
  //   15*0 12000000
endmodule
